// Logisim project 1bitalu.circ as structural Verilog: 1 circuit, main circuit main
module main (
  input  A,
  input  B,
  input  B_inv,
  input  Cin,
  input  Sel_1,
  input  Sel_0,
  output out_7,
  output out_8
);

  wire and_1_out, and_2_out, and_3_out, and_4_out, and_5_out, and_6_out, not_1_out, not_2_out, or_1_out,
       xor_1_out, xor_2_out, xor_3_out;

  xor xor_1 (xor_1_out, B, B_inv);
  not not_1 (not_1_out, Sel_1);
  not not_2 (not_2_out, Sel_0);
  and and_1 (and_1_out, A, xor_1_out);
  or or_1 (or_1_out, A, xor_1_out);
  xor xor_2 (xor_2_out, A, xor_1_out);
  and and_2 (and_2_out, A, xor_1_out);
  and and_3 (and_3_out, and_1_out, not_1_out, not_2_out);
  and and_4 (and_4_out, or_1_out, Sel_0, not_1_out);
  xor xor_3 (xor_3_out, xor_2_out, Cin);
  and and_5 (and_5_out, xor_2_out, Cin);
  or or_2 (out_7, and_2_out, and_5_out);
  and and_6 (and_6_out, xor_3_out, Sel_1, not_2_out);
  or or_3 (out_8, and_4_out, and_3_out, and_6_out);

  // Notes on the sheet:
  //     bx
  //                                                      1 BIT ALU_6563
  //   and_0
  //   or_0
  //   x1
  //   SUM
  //   Cout
  //   RESULT
endmodule
