// Logisim project 32_Bit_RISCV_Module.circ as structural Verilog: 1 circuit, main circuit main
module main (
  input  reset,
  output [31:0] PC,
  output [31:0] Instruction
);

  wire clock_1_out;
  wire [31:0] adder_1_out;

  Clock clock_1 (.out(clock_1_out));
  Register #(.width(32)) register_1 (.D(adder_1_out), .Q(PC), .clk(clock_1_out), .clr(reset));  // open: en
  Adder #(.width(32)) adder_1 (.a(PC), .b(32'h4), .out(adder_1_out));  // open: cin, cout
  ROM #(.addrWidth(4), .dataWidth(32)) rom_1 (.addr(PC[3:0]), .data(Instruction), .sel(1'b1));

  // Notes on the sheet:
  //   Constant
  //   6563
  //   6563
  //   Adder
  //   Register
  //   Clock
  //   Splitter
  //   32 BIT RISC V PC AND IM MODULE
  //   ROM
  //   contents of rom_1 (hex, n*v repeats v):
  //   100093 0 0 0 200113 0 0 0 2081b3 0 0 0 13
endmodule
