// Logisim project 32bitalu.circ as structural Verilog: 1 circuit, main circuit main
module main (
  input  [31:0] in_1,
  input  [31:0] in_2,
  input  [3:0] alu_op,
  output [31:0] out_4,
  output zero
);

  wire comparator_1_lt, comparator_2_lt;
  wire [4:0] shamt;
  wire [31:0] adder_1_out, and_1_out, bit_extender_2_out, bit_extender_3_out, or_1_out, shifter_1_out,
       shifter_2_out, shifter_3_out, subtractor_1_out, xor_1_out, zero32;

  Adder #(.width(32)) adder_1 (.a(in_1), .b(in_2), .out(adder_1_out));  // open: cin, cout
  Subtractor #(.width(32)) subtractor_1 (.a(in_1), .b(in_2), .out(subtractor_1_out));  // open: bin, bout
  assign and_1_out = in_1 & in_2;  // AND_Gate and_1, 32 bits wide
  assign or_1_out = in_1 | in_2;  // OR_Gate or_1, 32 bits wide
  assign xor_1_out = in_1 ^ in_2;  // XOR_Gate xor_1, 32 bits wide
  Comparator #(.width(32)) comparator_1 (.a(in_1), .b(in_2), .lt(comparator_1_lt));  // open: gt, eq
  Comparator #(.width(32), .mode("unsigned")) comparator_2 (.a(in_1), .b(in_2), .lt(comparator_2_lt));  // open: gt, eq
  Bit_Extender #(.in_width(32), .out_width(5)) bit_extender_1 (.in(in_2), .out(shamt));
  Shifter #(.width(32)) shifter_1 (.in(in_1), .\dist (shamt), .out(shifter_1_out));
  Shifter #(.width(32), .shift("lr")) shifter_2 (.in(in_1), .\dist (shamt), .out(shifter_2_out));
  Shifter #(.width(32), .shift("ar")) shifter_3 (.in(in_1), .\dist (shamt), .out(shifter_3_out));
  assign bit_extender_2_out = {{31{1'b0}}, comparator_1_lt};  // Bit_Extender bit_extender_2
  assign bit_extender_3_out = {{31{1'b0}}, comparator_2_lt};  // Bit_Extender bit_extender_3
  Multiplexer #(.select(4), .width(32)) multiplexer_1 (
    .in0(adder_1_out), .in1(subtractor_1_out), .in2(and_1_out), .in3(or_1_out), .in4(xor_1_out),
    .in5(bit_extender_2_out), .in6(bit_extender_3_out), .in7(shifter_1_out), .in8(shifter_2_out),
    .in9(shifter_3_out), .in10(zero32), .in11(zero32), .in12(zero32), .in13(zero32), .in14(zero32),
    .in15(zero32), .out(out_4), .sel(alu_op));  // open: en
  Comparator #(.width(32), .mode("unsigned")) comparator_3 (.a(out_4), .b({32{1'b0}}), .eq(zero));  // open: gt, lt

  // Other names for the same wires on the sheet: a[31:0] = in_1; b[31:0] = in_2; res[31:0] = out_4
endmodule
